# Fritzing sketch PIR_RF433_Broadcat (saved by Fritzing 0.8.7b)
breadboards: 1

parts:
  Part1 = Arduino Nano (Rev3.0)
  U1 = FS1000A - 433Mhz RF Transmitter [package=THT]
  PIR1 = PIR sensor
  R1 = Resistor [package="2010 [SMD]"]  # not connected
  LED1 = LED - 5mm [color="Green (555nm)" package="5 mm [THT]"]
  R2 = Resistor [package="2010 [SMD]"]
  VCC1 = Battery block 9V

nets:
  GND: Part1.GND, U1.GND, PIR1.GND, LED1.cathode, VCC1.-
  N1: Part1.D3, R2.Pin_1
  N2: Part1.D5, U1.DATA
  N3: Part1.VIN, VCC1.+
  5V: Part1.5V, U1.VCC, PIR1.VDD

custom parts:
  FS1000A - 433Mhz RF Transmitter: This is 433Mhz RF transmitter with receiver kit for Arduino ARM MCU wireless Application environment: Remote control switch, receiver module, motorcycles, automobile anti-theft products, home security products, electric doors, shutter doors, windows, remote control socket, remote control LED, remote audio remote control electric doors, garage door remote control, remote control retractable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
