# Fritzing sketch RF433_to_MQTT (saved by Fritzing 0.8.7b)

parts:
  WeMos_D1_Mini1 = WeMos D1 Mini
  U1 = RF-LINK_RX [package=rf-link_rx]

nets:
  5V: WeMos_D1_Mini1.5V, U1.+5V
  N1: WeMos_D1_Mini1.D4, U1.DATA
  N2: WeMos_D1_Mini1.G, U1.GND
